# Fritzing sketch scambiatoredicalore_circuit (saved by Fritzing 0.8.7b)
breadboards: 2

parts:
  Componente1 = Real Time Clock Module - DS1307 RTC Breakout Board
  Componente2 = Arduino Nano (Rev3.0)
  RHT1 = Humidity and Temperature Sensor RHT03
  U1 = RELAY [package=relay-jzc]
  LED1 = RGB LED (com. anode, rbg) [package="5 mm [THT]"]

nets:
  5V: Componente1.5V, Componente2.5V, RHT1.Vcc
  GND: Componente1.GND, Componente2.GND, RHT1.GND_1, U1.MAIN, LED1.common_anode
  N1: Componente1.SCL, Componente2.A5
  N2: Componente1.SDA, Componente2.A4
  N3: Componente2.D9, RHT1.Data-signal
  N4: Componente2.D10, U1.COIL1
  N5: Componente2.D11/MOSI, LED1.blue_cathode
  N6: Componente2.D12/MISO, LED1.red_cathode
